# Fritzing sketch fichinaMKII (saved by Fritzing 0.9.3b)
breadboards: 1

parts:
  J6 = male pin header, 6 pins [form="♂ (male)"]
  1N4007 = Rectifier Diode [part_number=1N4007 package="300 mil [THT]"]
  22pF = Ceramic Capacitor [capacitance=100nF package="100 mil [THT, multilayer]"]
  22pF_2 = Ceramic Capacitor [capacitance=10pF package="100 mil [THT, multilayer]"]
  0_1uF = Ceramic Capacitor [capacitance=100nF package="200 mil [THT, multilayer]"]
  RST = Pushbutton [package="[THT]"]
  10K = Resistor [tolerance=±5% resistance=10k package=THT]
  100uF = Electrolytic Capacitor [capacitance=47µF voltage=20V package="100 mil [THT, electrolytic]"]
  100uF_2 = Electrolytic Capacitor [capacitance=47µF voltage=20V package="100 mil [THT, electrolytic]"]
  ATMEGA328P = atmega328 [part_number="ATMEGA 328" package=dip]
  16Mhz = Crystal [frequency="16 Mhz" package=THT]
  D3 = Rectifier Diode [part_number=1N4148 package="300 mil [THT]"]
  D4 = Rectifier Diode [part_number=1N4001 package="300 mil [THT]"]
  1k1 = Resistor [tolerance=±5% resistance=1k package=THT]
  330ohm1 = Resistor [tolerance=±5% resistance=330 package=THT]
  R6 = Resistor [tolerance=±5% resistance=330 package=THT]
  JP3 = RCA [package=rca_lock]
  JP4 = RCA [package=rca_lock]
  R7 = Resistor [tolerance=±5% resistance=3.3 package=THT]
  U1 = Voltage Regulator - 5V [package="TO220 [THT]"]  # not connected
  U2 = Voltage Regulator - 5V [package="TO220 [THT]"]  # not connected

nets:
  N1: J6.pin1, 0_1uF.1
  N2: J6.pin2, ATMEGA328P.D1_(TX)
  N3: J6.pin3, ATMEGA328P.D0_(RX)
  N4: J6.pin6, 22pF.0, 22pF_2.1, 0_1uF.0, RST.Pin_1, RST.Pin_2, 10K.Pin_0, 100uF.+, ATMEGA328P.RESET, ATMEGA328P.GND
  N5: 1N4007.cathode, 100uF_2.+
  N6: 22pF.1, ATMEGA328P.XLAT1, 16Mhz.pin_1
  N7: 22pF_2.0, ATMEGA328P.XLAT2, 16Mhz.pin_0
  N8: 10K.Pin_1, ATMEGA328P.VCC, ATMEGA328P.AVCC
  N9: 100uF.-, 100uF_2.-
  N10: ATMEGA328P.D7, D3.anode
  N11: ATMEGA328P.D9_(PWM), D4.anode
  N12: ATMEGA328P.D11_(PWM), R6.Pin_1
  N13: D3.cathode, 330ohm1.Pin_1
  N14: D4.cathode, 1k1.Pin_1
  N15: 1k1.Pin_0, 330ohm1.Pin_0, R6.Pin_0, JP3.PIN, JP3.SWITCH, JP4.PIN, JP4.SWITCH, R7.Pin_0, R7.Pin_1

notes:
  GND
  laboratoriodejuguete.com, FATTO IN CASA , 2
  DTR
  5V
  TX
  RX
